# Fritzing sketch iPi-Addr (saved by Fritzing 0.9.3b)
breadboards: 1

parts:
  Raspberry_Pi_1 = Raspberry Pi 3 [part_number=RPI-3-V1.2]
  S1 = Pushbutton [package="[THT]"]
  LCM1602_IIC2 = LCM1602 IIC [part_number="LCM1602 IIC" chip_label="LCM1602 IIC" package="DIP (Dual Inline) [THT]"]
  LCD1 = LCD screen
  R1 = Resistor [tolerance=±5% resistance=220 package=THT]

nets:
  N1: Raspberry_Pi_1.3v3, S1.Pin_3, S1.Pin_4
  N2: Raspberry_Pi_1.GPIO2, LCM1602_IIC2.SDA
  N3: Raspberry_Pi_1.GPIO3, LCM1602_IIC2.SCL
  N4: Raspberry_Pi_1.GPIO25, S1.Pin_1, S1.Pin_2, R1.Pin_0
  GND: Raspberry_Pi_1.GND, LCM1602_IIC2.GND, R1.Pin_1
  5V: Raspberry_Pi_1.5V, LCM1602_IIC2.VCC
  VSS: LCM1602_IIC2.VSS, LCD1.VSS
  VDD: LCM1602_IIC2.VDD, LCD1.VDD
  N5: LCM1602_IIC2.V0, LCD1.V0
  N6: LCM1602_IIC2.RS, LCD1.RS
  N7: LCM1602_IIC2.RW, LCD1.R/W
  N8: LCM1602_IIC2.E, LCD1.E
  N9: LCM1602_IIC2.D0, LCD1.DB0
  N10: LCM1602_IIC2.D1, LCD1.DB1
  N11: LCM1602_IIC2.D2, LCD1.DB2
  N12: LCM1602_IIC2.D3, LCD1.DB3
  N13: LCM1602_IIC2.D4, LCD1.DB4
  N14: LCM1602_IIC2.D5, LCD1.DB5
  N15: LCM1602_IIC2.D6, LCD1.DB6
  N16: LCM1602_IIC2.D7, LCD1.DB7
  N17: LCM1602_IIC2.A, LCD1.LED+
  N18: LCM1602_IIC2.K, LCD1.LED-
  N19: LCM1602_IIC2.LED_A, LCM1602_IIC2.LED_B

custom parts:
  LCM1602 IIC: I2C-Module to use a 1602 or 2004 LCD on with the wire.h libory Serial LCD Modul
